// Digital circuit 2digitBCDtobinary.dig as structural Verilog
module _2digitBCDtobinary (
  input  [3:0] H,
  input  [3:0] L,
  output [6:0] _7bout
);

  wire [6:0] add_1_s;

  Add #(.Bits(7)) add_1 (.a({H, 3'b000}), .b({2'b00, H, 1'b0}), .c_i(1'b0), .s(add_1_s));  // open: c_o
  Add #(.Bits(7)) add_2 (.a(add_1_s), .b({3'b000, L}), .c_i(1'b0), .s(_7bout));  // open: c_o
endmodule
