// Digital circuit 4bitregister.dig as structural Verilog
module _4bitregister (
  input  clk,
  input  clr,
  input  [3:0] D,
  input  en,
  output [3:0] Q
);

  wire multiplexer_1_out, multiplexer_2_out, multiplexer_3_out, multiplexer_4_out;

  Multiplexer multiplexer_1 (.sel(en), .in_0(Q[0]), .in_1(D[0]), .out(multiplexer_1_out));
  D_FF_AS d_ff_as_1 (.Set(1'b0), .D(multiplexer_1_out), .C(clk), .Clr(clr), .Q(Q[0]));  // open: nQ
  Multiplexer multiplexer_2 (.sel(en), .in_0(Q[1]), .in_1(D[1]), .out(multiplexer_2_out));
  D_FF_AS d_ff_as_2 (.Set(1'b0), .D(multiplexer_2_out), .C(clk), .Clr(clr), .Q(Q[1]));  // open: nQ
  Multiplexer multiplexer_3 (.sel(en), .in_0(Q[2]), .in_1(D[2]), .out(multiplexer_3_out));
  D_FF_AS d_ff_as_3 (.Set(1'b0), .D(multiplexer_3_out), .C(clk), .Clr(clr), .Q(Q[2]));  // open: nQ
  Multiplexer multiplexer_4 (.sel(en), .in_0(Q[3]), .in_1(D[3]), .out(multiplexer_4_out));
  D_FF_AS d_ff_as_4 (.Set(1'b0), .D(multiplexer_4_out), .C(clk), .Clr(clr), .Q(Q[3]));  // open: nQ
endmodule
