// Digital circuit 7bitregister.dig as structural Verilog
module _7bitregister (
  input  clk,
  input  clr,
  input  [6:0] D,
  input  en,
  output [6:0] Q
);

  wire delay_1_out, multiplexer_1_out, multiplexer_2_out, multiplexer_3_out, multiplexer_4_out,
       multiplexer_5_out, multiplexer_6_out, multiplexer_7_out;

  Multiplexer multiplexer_1 (.sel(en), .in_0(Q[0]), .in_1(D[0]), .out(multiplexer_1_out));
  Delay delay_1 (.in(clk), .out(delay_1_out));
  D_FF_AS d_ff_as_1 (.Set(1'b0), .D(multiplexer_1_out), .C(delay_1_out), .Clr(clr), .Q(Q[0]));  // open: nQ
  Multiplexer multiplexer_2 (.sel(en), .in_0(Q[1]), .in_1(D[1]), .out(multiplexer_2_out));
  D_FF_AS d_ff_as_2 (.Set(1'b0), .D(multiplexer_2_out), .C(delay_1_out), .Clr(clr), .Q(Q[1]));  // open: nQ
  Multiplexer multiplexer_3 (.sel(en), .in_0(Q[2]), .in_1(D[2]), .out(multiplexer_3_out));
  D_FF_AS d_ff_as_3 (.Set(1'b0), .D(multiplexer_3_out), .C(delay_1_out), .Clr(clr), .Q(Q[2]));  // open: nQ
  D_FF_AS d_ff_as_4 (.Set(1'b0), .D(multiplexer_4_out), .C(delay_1_out), .Clr(clr), .Q(Q[3]));  // open: nQ
  Multiplexer multiplexer_4 (.sel(en), .in_0(Q[3]), .in_1(D[3]), .out(multiplexer_4_out));
  Multiplexer multiplexer_5 (.sel(en), .in_0(Q[4]), .in_1(D[4]), .out(multiplexer_5_out));
  D_FF_AS d_ff_as_5 (.Set(1'b0), .D(multiplexer_5_out), .C(delay_1_out), .Clr(clr), .Q(Q[4]));  // open: nQ
  Multiplexer multiplexer_6 (.sel(en), .in_0(Q[5]), .in_1(D[5]), .out(multiplexer_6_out));
  D_FF_AS d_ff_as_6 (.Set(1'b0), .D(multiplexer_6_out), .C(delay_1_out), .Clr(clr), .Q(Q[5]));  // open: nQ
  Multiplexer multiplexer_7 (.sel(en), .in_0(Q[6]), .in_1(D[6]), .out(multiplexer_7_out));
  D_FF_AS d_ff_as_7 (.Set(1'b0), .D(multiplexer_7_out), .C(delay_1_out), .Clr(clr), .Q(Q[6]));  // open: nQ
endmodule
