// Digital circuit Bin to BCD.dig as structural Verilog
module Bin_to_BCD (
  input  [6:0] bin,
  output [7:0] bcd
);

  wire conditional_adder_1_out0, conditional_adder_1_out1, conditional_adder_1_out2,
       conditional_adder_2_out0, conditional_adder_2_out1, conditional_adder_2_out2,
       conditional_adder_3_out0, conditional_adder_3_out1, conditional_adder_3_out2;

  conditional_adder conditional_adder_1 (
    .out0(conditional_adder_1_out0), .out1(conditional_adder_1_out1), .out2(conditional_adder_1_out2),
    .out3(bcd[7]), ._0(bin[4]), ._1(bin[5]), ._2(bin[6]), ._3(1'b0));
  conditional_adder conditional_adder_2 (
    .out0(conditional_adder_2_out0), .out1(conditional_adder_2_out1), .out2(conditional_adder_2_out2),
    .out3(bcd[6]), ._0(bin[3]), ._1(conditional_adder_1_out0), ._2(conditional_adder_1_out1),
    ._3(conditional_adder_1_out2));
  conditional_adder conditional_adder_3 (
    .out0(conditional_adder_3_out0), .out1(conditional_adder_3_out1), .out2(conditional_adder_3_out2),
    .out3(bcd[5]), ._0(bin[2]), ._1(conditional_adder_2_out0), ._2(conditional_adder_2_out1),
    ._3(conditional_adder_2_out2));
  conditional_adder conditional_adder_4 (
    .out0(bcd[1]), .out1(bcd[2]), .out2(bcd[3]), .out3(bcd[4]), ._0(bin[1]), ._1(conditional_adder_3_out0),
    ._2(conditional_adder_3_out1), ._3(conditional_adder_3_out2));

  assign bcd[0] = bin[0];
endmodule
