// Digital circuit calc.dig as structural Verilog
module calc (
);

  wire _0, _1, _2, _3, _4, _5, _6, _7, _8, _9, add_1_c_o, and_1_out, and_2_out, and_3_out, and_4_out,
       and_5_out, and_6_out, C, comparator_1_lt, comparator_2_lt, d_ff_1_q, decoder_1_out_0, decoder_1_out_1,
       decoder_1_out_2, del, delay_1_out, delay_2_out, eq, not_1_out, or_1_out, or_2_out, or_3_out, or_4_out,
       or_5_out, or_8_out, or_9_out, or_10_out, or_11_out, plus, priorityencoder_1_any, sub_1_c_o, tunnel,
       tunnel_t, X;
  wire [0:0] digit_counter_1_out;
  wire [1:0] or_7_out, register_1_q;
  wire [3:0] multiplexer_1_out, multiplexer_2_out, priorityencoder_1_num, reg1_q, reg2_q;
  wire [6:0] _2digitbcdtobinary_1__7bout, _7bitregister_1_q, add_1_s, binto7seg_1_a, binto7seg_2_a, div_1_q,
       multiplexer_3_out, multiplexer_4_out, sub_1_s;
  wire [7:0] bin_to_bcd_1_bcd;
  wire [13:0] mul_1_mul, multiplexer_5_out;

  Button u__7 (.out(_7));
  Button u__4 (.out(_4));
  Button u__1 (.out(_1));
  Button u_del (.out(del));
  Button u__8 (.out(_8));
  Button u__5 (.out(_5));
  Button u__2 (.out(_2));
  Button u__0 (.out(_0));
  Button u_C (.out(C));
  Button u__9 (.out(_9));
  Button u__6 (.out(_6));
  Button u__3 (.out(_3));
  Button u_eq (.out(eq));
  Button button (.out(tunnel_t));
  Button u_X (.out(X));
  Button button_2 (.out(tunnel));
  Button u_plus (.out(plus));
  PriorityEncoder #(.Selector_Bits(4)) priorityencoder_1 (
    .in0(_0), .in1(_1), .in2(_2), .in3(_3), .in4(_4), .in5(_5), .in6(_6), .in7(_7), .in8(_8), .in9(_9),
    .in10(1'b0), .in11(1'b0), .in12(1'b0), .in13(1'b0), .in14(1'b0), .in15(1'b0),
    .num(priorityencoder_1_num), .any(priorityencoder_1_any));
  or or_1 (or_1_out, priorityencoder_1_any, del);
  or or_2 (or_2_out, priorityencoder_1_any, 1'b0);
  Delay delay_1 (.in(or_1_out), .out(delay_1_out));
  and and_1 (and_1_out, eq, 1'b1);
  digit_counter digit_counter_1 (
    .clk(delay_1_out), .clr(or_4_out), .up_down(or_2_out), .set(1'b0), .out(digit_counter_1_out[0]));
  or or_3 (or_3_out, priorityencoder_1_any, and_1_out, del);
  or or_4 (or_4_out, plus, tunnel, C, X, tunnel_t);
  or or_5 (or_5_out, or_4_out, del);
  Delay delay_2 (.in(or_3_out), .out(delay_2_out));
  Multiplexer #(.Bits(4)) multiplexer_1 (
    .sel(eq), .in_0(reg2_q), .in_1(bin_to_bcd_1_bcd[7:4]), .out(multiplexer_1_out));
  Multiplexer #(.Selector_Bits(2), .Bits(4)) multiplexer_2 (
    .sel({eq, digit_counter_1_out[0]}), .in_0(reg1_q), .in_1(priorityencoder_1_num),
    .in_2(bin_to_bcd_1_bcd[3:0]), .in_3(bin_to_bcd_1_bcd[3:0]), .out(multiplexer_2_out));
  or or_6 (or_7_out[0], tunnel, tunnel_t);
  or or_7 (or_7_out[1], X, tunnel_t);
  or or_8 (or_8_out, digit_counter_1_out[0], eq, del);
  _4bitregister reg1 (.clk(delay_2_out), .clr(or_5_out), .D(multiplexer_1_out), .en(or_8_out), .Q(reg1_q));
  _4bitregister reg2 (.clk(delay_2_out), .clr(or_4_out), .D(multiplexer_2_out), .en(or_8_out), .Q(reg2_q));
  // Probe on reg2_q
  and and_2 (and_2_out, eq, not_1_out);
  binto7seg binto7seg_1 (
    .Q3(reg1_q[3]), .Q2(reg1_q[2]), .Q1(reg1_q[1]), .Q0(reg1_q[0]), .a(binto7seg_1_a[0]),
    .b(binto7seg_1_a[1]), .c(binto7seg_1_a[2]), .d(binto7seg_1_a[3]), .e(binto7seg_1_a[4]),
    .f(binto7seg_1_a[5]), .g(binto7seg_1_a[6]));
  binto7seg binto7seg_2 (
    .Q3(reg2_q[3]), .Q2(reg2_q[2]), .Q1(reg2_q[1]), .Q0(reg2_q[0]), .a(binto7seg_2_a[0]),
    .b(binto7seg_2_a[1]), .c(binto7seg_2_a[2]), .d(binto7seg_2_a[3]), .e(binto7seg_2_a[4]),
    .f(binto7seg_2_a[5]), .g(binto7seg_2_a[6]));
  _2digitBCDtobinary _2digitbcdtobinary_1 (.H(reg1_q), .L(reg2_q), ._7bout(_2digitbcdtobinary_1__7bout));
  Multiplexer #(.Bits(7)) multiplexer_3 (
    .sel(d_ff_1_q), .in_0(binto7seg_1_a), .in_1(7'b1111001), .out(multiplexer_3_out));
  or or_9 (or_9_out, and_2_out, C);
  Register #(.Bits(2)) register_1 (.D(or_7_out), .C(or_4_out), .en(or_4_out), .Q(register_1_q));
  Multiplexer #(.Bits(7)) multiplexer_4 (
    .sel(d_ff_1_q), .in_0(binto7seg_2_a), .in_1(7'b1110111), .out(multiplexer_4_out));
  Seven_Seg seven_seg_1 (
    .a(multiplexer_3_out[0]), .b(multiplexer_3_out[1]), .c(multiplexer_3_out[2]), .d(multiplexer_3_out[3]),
    .e(multiplexer_3_out[4]), .f(multiplexer_3_out[5]), .g(multiplexer_3_out[6]), .dp(1'b0));
  Seven_Seg seven_seg_2 (
    .a(multiplexer_4_out[0]), .b(multiplexer_4_out[1]), .c(multiplexer_4_out[2]), .d(multiplexer_4_out[3]),
    .e(multiplexer_4_out[4]), .f(multiplexer_4_out[5]), .g(multiplexer_4_out[6]), .dp(1'b0));
  and and_3 (and_3_out, or_11_out, eq);
  D_FF d_ff_1 (.D(and_3_out), .C(or_9_out), .Q(d_ff_1_q));  // open: nQ
  _7bitregister _7bitregister_1 (
    .clk(or_4_out), .clr(C), .D(_2digitbcdtobinary_1__7bout), .en(or_4_out), .Q(_7bitregister_1_q));
  not not_1 (not_1_out, d_ff_1_q);
  Add #(.Bits(7)) add_1 (
    .a(_7bitregister_1_q), .b(_2digitbcdtobinary_1__7bout), .c_i(1'b0), .s(add_1_s), .c_o(add_1_c_o));
  Sub #(.Bits(7)) sub_1 (
    .a(_7bitregister_1_q), .b(_2digitbcdtobinary_1__7bout), .c_i(1'b0), .s(sub_1_s), .c_o(sub_1_c_o));
  Mul #(.Bits(7)) mul_1 (.a(_7bitregister_1_q), .b(_2digitbcdtobinary_1__7bout), .mul(mul_1_mul));
  Div #(.Bits(7)) div_1 (.a(_7bitregister_1_q), .b(_2digitbcdtobinary_1__7bout), .q(div_1_q));  // open: r
  Bin_to_BCD bin_to_bcd_1 (.bin(multiplexer_5_out[6:0]), .bcd(bin_to_bcd_1_bcd));
  Multiplexer #(.Selector_Bits(2), .Bits(14)) multiplexer_5 (
    .sel(register_1_q), .in_0({{7{1'b0}}, add_1_s}), .in_1({{7{1'b0}}, sub_1_s}), .in_2(mul_1_mul),
    .in_3({{7{1'b0}}, div_1_q}), .out(multiplexer_5_out));
  Decoder #(.Selector_Bits(2)) decoder_1 (
    .sel(register_1_q), .out_0(decoder_1_out_0), .out_1(decoder_1_out_1), .out_2(decoder_1_out_2));  // open: out_3
  Comparator #(.Bits(7)) comparator_1 (.a(7'b1100011), .b(add_1_s), .lt(comparator_1_lt));  // open: gt, eq
  Comparator #(.Bits(14)) comparator_2 (.a(14'h63), .b(mul_1_mul), .lt(comparator_2_lt));  // open: gt, eq
  or or_10 (or_10_out, comparator_1_lt, add_1_c_o);
  and and_4 (and_4_out, decoder_1_out_0, or_10_out);
  and and_5 (and_5_out, decoder_1_out_1, sub_1_c_o);
  and and_6 (and_6_out, decoder_1_out_2, comparator_2_lt);
  or or_11 (or_11_out, and_4_out, and_5_out, and_6_out);

  // Notes on the sheet:
  //   2 digit Calculator
endmodule
