// Digital circuit conditional adder.dig as structural Verilog
module conditional_adder (
  input  _0,
  input  _1,
  input  _2,
  input  _3,
  output out0,
  output out1,
  output out2,
  output out3
);

  wire comparator_1_lt;
  wire [3:0] add_1_s;

  Comparator #(.Bits(4)) comparator_1 (.a(4'b0100), .b({_3, _2, _1, _0}), .lt(comparator_1_lt));  // open: gt, eq
  Add #(.Bits(4)) add_1 (.a({_3, _2, _1, _0}), .b(4'b0011), .c_i(1'b0), .s(add_1_s));  // open: c_o
  Multiplexer #(.Bits(4)) multiplexer_1 (
    .sel(comparator_1_lt), .in_0({_3, _2, _1, _0}), .in_1(add_1_s), .out({out3, out2, out1, out0}));
endmodule
