// Digital circuit digit_counter.dig as structural Verilog
module digit_counter (
  input  clk,
  input  clr,
  input  up_down,
  input  set,
  output out
);

  wire and_1_out, d_ff_as_1_q, d_ff_as_2_q, or_1_out;

  or or_1 (or_1_out, up_down, d_ff_as_2_q);
  D_FF_AS d_ff_as_1 (.Set(set), .D(or_1_out), .C(clk), .Clr(clr), .Q(d_ff_as_1_q));  // open: nQ
  and and_1 (and_1_out, up_down, d_ff_as_1_q);
  D_FF_AS d_ff_as_2 (.Set(set), .D(and_1_out), .C(clk), .Clr(clr), .Q(d_ff_as_2_q));  // open: nQ
  nand nand_1 (out, d_ff_as_1_q, d_ff_as_2_q);
endmodule
